# Fritzing sketch DHT22 (saved by Fritzing 0.9.0b)
circuit board: 8.46667cm x 5.64444cm
breadboards: 1

parts:
  Componente1 = Arduino Nano (Rev3.0)
  DHT1 = DHT22 Humidity and Temperature Sensor

nets:
  GND: Componente1.GND, DHT1.GND
  N1: Componente1.D2, DHT1.DATA
  5V: Componente1.5V, DHT1.VDD

notes:
  Using DHT22 breakout with 5.1k pullup resistor
