# Fritzing sketch DHT22_Logger (saved by Fritzing 0.9.1b)
circuit board: 8.46667cm x 5.64444cm
breadboards: 1

parts:
  SD_Shield = Memoire 1.0 - SD card log shield
  Arduino_UNO = Arduino Uno (Rev3)

nets (from the breadboard view):
  N1: SD_Shield.DIG_8, Arduino_UNO.D8
  N2: SD_Shield.DIG_9, Arduino_UNO.D9_PWM
  N3: SD_Shield.DIG_10, Arduino_UNO.D10_PWM/SS
  N4: SD_Shield.DIG_11, Arduino_UNO.D11_PWM/MOSI
  N5: SD_Shield.DIG_12, Arduino_UNO.D12/MISO
  N6: SD_Shield.DIG_13, Arduino_UNO.D13/SCK
  GND: SD_Shield.GND, Arduino_UNO.GND
  N7: SD_Shield.AREF, Arduino_UNO.AREF
  N8: SD_Shield.DIG_0, Arduino_UNO.D0/RX
  N9: SD_Shield.DIG_1, Arduino_UNO.D1/TX
  N10: SD_Shield.DIG_2, Arduino_UNO.D2
  N11: SD_Shield.DIG_3, Arduino_UNO.D3_PWM
  N12: SD_Shield.DIG_4, Arduino_UNO.D4
  N13: SD_Shield.DIG_5, Arduino_UNO.D5_PWM
  N14: SD_Shield.DIG_6, Arduino_UNO.D6_PWM
  N15: SD_Shield.DIG_7, Arduino_UNO.D7
  N16: SD_Shield.A_IN_0, Arduino_UNO.A0
  N17: SD_Shield.A_IN_1, Arduino_UNO.A1
  N18: SD_Shield.A_IN_2, Arduino_UNO.A2
  N19: SD_Shield.A_IN_3, Arduino_UNO.A3
  N20: SD_Shield.A_IN_4, Arduino_UNO.A4/SDA
  N21: SD_Shield.A_IN_5, Arduino_UNO.A5/SCL
  N22: SD_Shield.RESET, Arduino_UNO.RESET
  3V3: SD_Shield.3V3, Arduino_UNO.3V3
  +5V: SD_Shield.+5V, Arduino_UNO.5V
  VIN: SD_Shield.VIN, Arduino_UNO.VIN
